// Logisim project 2.7.circ as structural Verilog: 3 circuits, main circuit A
module A (
  input  A,
  input  B,
  input  C,
  output Y
);

  wire and_1_out, and_2_out, not_1_out;

  not not_1 (not_1_out, B);
  and and_1 (and_1_out, A, C);
  and and_2 (and_2_out, not_1_out, C);
  or or_1 (Y, and_1_out, and_2_out);
endmodule

module B (
  input  A,
  output Y
);

  not not_1 (Y, A);
endmodule

module c (
  input  A,
  input  B,
  input  C,
  input  D,
  output Y
);

  wire and_1_out, and_2_out, not_1_out, not_2_out, not_3_out, not_4_out;

  not not_1 (not_1_out, A);
  not not_2 (not_2_out, B);
  not not_3 (not_3_out, C);
  not not_4 (not_4_out, D);
  and and_1 (and_1_out, not_2_out, not_4_out);
  and and_2 (and_2_out, not_3_out, D);
  or or_1 (Y, not_1_out, and_1_out, and_2_out);
endmodule
