// Logisim project 2.9.circ as structural Verilog: 1 circuit, main circuit main
module main (
  input  A,
  input  B,
  input  C,
  input  D,
  input  E,
  output Y
);

  wire AB_out, ABC_out, AC_out, and_1_out, and_2_out, and_3_out, D_E_out, not_2_out, not_3_out, not_4_out,
       not_5_out, or_1_out;

  // NOT_Gate not_1 has open pins: in=A, out=open
  not not_2 (not_2_out, B);
  not not_3 (not_3_out, C);
  or D_E (D_E_out, D, E);
  and AB (AB_out, A, B);
  and AC (AC_out, A, C);
  and and_1 (and_1_out, not_2_out, not_3_out);
  not not_4 (not_4_out, D_E_out);
  and ABC (ABC_out, AB_out, AC_out);
  or or_1 (or_1_out, AB_out, AC_out, and_1_out);
  not not_5 (not_5_out, ABC_out);
  and and_2 (and_2_out, or_1_out, D_E_out);
  and and_3 (and_3_out, not_5_out, not_4_out);
  or or_2 (Y, ABC_out, and_2_out, and_3_out);
endmodule
