// Logisim project 4.4.1-2.circ as structural Verilog: 1 circuit, main circuit main
module main (
  input  A,
  input  C,
  input  B,
  input  a_2,
  input  b_2,
  input  c_2,
  output Output2,
  output Output1,
  output Output1_2,
  output Output2_2
);

  wire and_1_out, and_2_out, or_1_out, or_2_out, or_4_out, or_5_out, or_6_out, xor_1_out;

  or or_1 (or_1_out, A, B);
  or or_2 (or_2_out, a_2, b_2);
  xor xor_1 (xor_1_out, or_2_out, b_2);
  or or_3 (Output2, or_1_out, C);
  or or_4 (or_4_out, Output2, and_1_out);
  and and_1 (and_1_out, A, C);
  and and_2 (and_2_out, A, B);
  or or_5 (or_5_out, xor_1_out, or_6_out);
  or or_6 (or_6_out, a_2, c_2);
  and and_3 (Output2_2, a_2, b_2);
  or or_7 (Output1, or_4_out, and_2_out);
  or or_8 (Output1_2, or_5_out, Output2_2);
endmodule
