// Logisim project 4.5.1(use adder as library).circ as structural Verilog: 2 circuits, main circuit a.ont bit X+1
module a_ont_bit_X_1 (
  input  Start,
  input  Input,
  output out_3
);

  wire Clock_out, d_ff_2_q, Full_Adder_c2, Full_Adder_s;

  full_adder Full_Adder (.A(Input), .B(Start), .C1(d_ff_2_q), .S(Full_Adder_s), .C2(Full_Adder_c2));
  Clock Clock (.out(Clock_out));
  D_Flip_Flop d_ff_1 (.clk(Clock_out), .D(Full_Adder_s), .Q(out_3));  // open: Qn, preset, en, reset
  D_Flip_Flop d_ff_2 (.clk(Clock_out), .D(Full_Adder_c2), .Q(d_ff_2_q));  // open: Qn, preset, en, reset

  // Notes on the sheet:
  //   C
  //   S
endmodule

module b_one_bit_Shift_2 (
  input  \input ,
  input  Start,
  output Output
);

  wire Clock_out, d_ff_1_q, d_ff_2_q;

  Clock Clock (.out(Clock_out));
  D_Flip_Flop d_ff_1 (.clk(Clock_out), .D(\input ), .Q(d_ff_1_q));  // open: Qn, preset, en, reset
  D_Flip_Flop d_ff_2 (.clk(Clock_out), .D(d_ff_1_q), .Q(d_ff_2_q), .reset(Start));  // open: Qn, preset, en
  D_Flip_Flop d_ff_3 (.clk(Clock_out), .D(d_ff_2_q), .Q(Output), .reset(Start));  // open: Qn, preset, en
endmodule
