// Logisim project 4.5.2.circ as structural Verilog: 2 circuits, main circuit a
module a (
  input  Input0,
  input  Input1,
  input  Start,
  output output0,
  output output1
);

  wire Clock_out, d_ff_3_q, full_adder_1_c2, full_adder_1_s, full_adder_2_c2, full_adder_2_s;

  full_adder full_adder_1 (.A(Input0), .B(Start), .C1(d_ff_3_q), .S(full_adder_1_s), .C2(full_adder_1_c2));
  Clock Clock (.out(Clock_out));
  full_adder full_adder_2 (.A(1'b0), .B(Input1), .C1(full_adder_1_c2), .S(full_adder_2_s), .C2(full_adder_2_c2));
  D_Flip_Flop d_ff_1 (.clk(Clock_out), .D(full_adder_1_s), .Q(output0));  // open: Qn, preset, en, reset
  D_Flip_Flop d_ff_2 (.clk(Clock_out), .D(full_adder_2_s), .Q(output1));  // open: Qn, preset, en, reset
  D_Flip_Flop d_ff_3 (.clk(Clock_out), .D(full_adder_2_c2), .Q(d_ff_3_q));  // open: Qn, preset, en, reset
endmodule

module b (
  input  input0,
  input  Start,
  input  input1,
  output Output0,
  output Output1
);

  wire Clock_out, d_ff_1_q, d_ff_2_q;

  Clock Clock (.out(Clock_out));
  D_Flip_Flop d_ff_1 (.clk(Clock_out), .D(input0), .Q(d_ff_1_q));  // open: Qn, preset, en, reset
  D_Flip_Flop d_ff_2 (.clk(Clock_out), .D(input1), .Q(d_ff_2_q));  // open: Qn, preset, en, reset
  D_Flip_Flop d_ff_3 (.clk(Clock_out), .D(d_ff_1_q), .Q(Output0), .reset(Start));  // open: Qn, preset, en
  D_Flip_Flop d_ff_4 (.clk(Clock_out), .D(d_ff_2_q), .Q(Output1), .reset(Start));  // open: Qn, preset, en
  a a_1 ();  // open: Input0, Input1, Start, output0, output1
endmodule
