// Logisim project ALU.circ as structural Verilog: 5 circuits, main circuit ALU
module ALU (
  input  [31:0] inputA,
  input  [31:0] inputB,
  input  [1:0] ALUOp_1_0,
  output [31:0] result,
  output zero
);

  wire [31:0] bitwise_or_1_result, multiplexer_1_out, n32bit_adder_1_result, negativeb_1_result;

  negativeB negativeb_1 (.inputB(inputB), .result(negativeb_1_result));
  bitwise_OR bitwise_or_1 (.result(bitwise_or_1_result), .inputA(inputB), .inputB(inputA));
  compare compare_1 (.inputA(inputB), .inputB(inputA), .out_3(zero));
  _32bit_adder u_32bit_adder_1 (.inputA(inputA), .inputB(multiplexer_1_out), .result(n32bit_adder_1_result));
  Multiplexer #(.width(32), .enable("false")) multiplexer_1 (
    .in0(inputB), .in1(negativeb_1_result), .out(multiplexer_1_out), .sel(ALUOp_1_0[0]));
  Multiplexer #(.select(2), .width(32), .enable("false")) multiplexer_2 (
    .in0(n32bit_adder_1_result), .in1(n32bit_adder_1_result), .in2(bitwise_or_1_result), .in3(inputB),
    .out(result), .sel(ALUOp_1_0));
endmodule

module _32bit_adder (
  input  [31:0] inputA,
  input  [31:0] inputB,
  output [31:0] result
);

  wire n8bit_adder_2_cout, n8bit_adder_3_cout, n8bit_adder_4_cout;

  _8bit_adder u_8bit_adder_1 (
    .inputA(inputA[31:24]), .inputB(inputB[31:24]), .Cin(n8bit_adder_2_cout), .\output (result[31:24]));  // open: Cout
  _8bit_adder u_8bit_adder_2 (
    .inputA(inputA[23:16]), .inputB(inputB[23:16]), .Cout(n8bit_adder_2_cout), .Cin(n8bit_adder_3_cout),
    .\output (result[23:16]));
  _8bit_adder u_8bit_adder_3 (
    .inputA(inputA[15:8]), .inputB(inputB[15:8]), .Cout(n8bit_adder_3_cout), .Cin(n8bit_adder_4_cout),
    .\output (result[15:8]));
  _8bit_adder u_8bit_adder_4 (
    .inputA(inputA[7:0]), .inputB(inputB[7:0]), .Cout(n8bit_adder_4_cout), .Cin(1'b0), .\output (result[7:0]));
endmodule

module negativeB (
  input  [31:0] inputB,
  output [31:0] result
);

  wire [31:0] not_1_out;

  assign not_1_out = ~inputB;  // NOT_Gate not_1, 32 bits wide
  _32bit_adder u_32bit_adder_1 (.inputA(not_1_out), .inputB(32'h1), .result(result));
endmodule

module bitwise_OR (
  input  [31:0] inputA,
  input  [31:0] inputB,
  output [31:0] result
);

  or or_1 (result[30], inputA[30], inputB[30]);
  or or_2 (result[28], inputA[28], inputB[28]);
  or or_3 (result[26], inputA[26], inputB[26]);
  or or_4 (result[24], inputA[24], inputB[24]);
  or or_5 (result[22], inputA[22], inputB[22]);
  or or_6 (result[20], inputA[20], inputB[20]);
  or or_7 (result[18], inputA[18], inputB[18]);
  or or_8 (result[16], inputA[16], inputB[16]);
  or or_9 (result[14], inputA[14], inputB[14]);
  or or_10 (result[12], inputA[12], inputB[12]);
  or or_11 (result[10], inputA[10], inputB[10]);
  or or_12 (result[8], inputA[8], inputB[8]);
  or or_13 (result[6], inputA[6], inputB[6]);
  or or_14 (result[4], inputA[4], inputB[4]);
  or or_15 (result[2], inputA[2], inputB[2]);
  or or_16 (result[0], inputA[0], inputB[0]);
  or or_17 (result[31], inputA[31], inputB[31]);
  or or_18 (result[29], inputA[29], inputB[29]);
  or or_19 (result[27], inputA[27], inputB[27]);
  or or_20 (result[25], inputA[25], inputB[25]);
  or or_21 (result[23], inputA[23], inputB[23]);
  or or_22 (result[21], inputA[21], inputB[21]);
  or or_23 (result[19], inputA[19], inputB[19]);
  or or_24 (result[17], inputA[17], inputB[17]);
  or or_25 (result[15], inputA[15], inputB[15]);
  or or_26 (result[13], inputA[13], inputB[13]);
  or or_27 (result[11], inputA[11], inputB[11]);
  or or_28 (result[9], inputA[9], inputB[9]);
  or or_29 (result[7], inputA[7], inputB[7]);
  or or_30 (result[5], inputA[5], inputB[5]);
  or or_31 (result[3], inputA[3], inputB[3]);
  or or_32 (result[1], inputA[1], inputB[1]);

  // Other names for the same wires on the sheet: A00 = inputA[0]; A01 = inputA[1]; A02 = inputA[2]; A03 = inputA[3];
  //   A04 = inputA[4]; A05 = inputA[5]; A06 = inputA[6]; A07 = inputA[7]; A08 = inputA[8]; A09 = inputA[9];
  //   A10 = inputA[10]; A11 = inputA[11]; A12 = inputA[12]; A13 = inputA[13]; A14 = inputA[14]; A15 = inputA[15];
  //   A16 = inputA[16]; A17 = inputA[17]; A18 = inputA[18]; A19 = inputA[19]; A20 = inputA[20]; A21 = inputA[21];
  //   A22 = inputA[22]; A23 = inputA[23]; A24 = inputA[24]; A25 = inputA[25]; A26 = inputA[26]; A27 = inputA[27];
  //   A28 = inputA[28]; A29 = inputA[29]; A30 = inputA[30]; A31 = inputA[31]; B00 = inputB[0]; B01 = inputB[1];
  //   B02 = inputB[2]; B03 = inputB[3]; B04 = inputB[4]; B05 = inputB[5]; B06 = inputB[6]; B07 = inputB[7];
  //   B08 = inputB[8]; B09 = inputB[9]; B10 = inputB[10]; B11 = inputB[11]; B12 = inputB[12]; B13 = inputB[13];
  //   B14 = inputB[14]; B15 = inputB[15]; B16 = inputB[16]; B17 = inputB[17]; B18 = inputB[18]; B19 = inputB[19];
  //   B20 = inputB[20]; B21 = inputB[21]; B22 = inputB[22]; B23 = inputB[23]; B24 = inputB[24]; B25 = inputB[25];
  //   B26 = inputB[26]; B27 = inputB[27]; B28 = inputB[28]; B29 = inputB[29]; B30 = inputB[30]; B31 = inputB[31];
  //   C00 = result[0]; C01 = result[1]; C02 = result[2]; C03 = result[3]; C04 = result[4]; C05 = result[5];
  //   C06 = result[6]; C07 = result[7]; C08 = result[8]; C09 = result[9]; C10 = result[10]; C11 = result[11];
  //   C12 = result[12]; C13 = result[13]; C14 = result[14]; C15 = result[15]; C16 = result[16]; C17 = result[17];
  //   C18 = result[18]; C19 = result[19]; C20 = result[20]; C21 = result[21]; C22 = result[22]; C23 = result[23];
  //   C24 = result[24]; C25 = result[25]; C26 = result[26]; C27 = result[27]; C28 = result[28]; C29 = result[29];
  //   C30 = result[30]; C31 = result[31]
endmodule

module compare (
  input  [31:0] inputA,
  input  [31:0] inputB,
  output out_3
);

  wire C00, C01, C02, C03, C04, C05, C06, C07, C08, C09, C10, C11, C12, C13, C14, C15, C16, C17, C18, C19,
       C20, C21, C22, C23, C24, C25, C26, C27, C28, C29, C30, C31, or_1_out;

  xor xor_1 (C30, inputA[30], inputB[30]);
  xor xor_2 (C28, inputA[28], inputB[28]);
  xor xor_3 (C26, inputA[26], inputB[26]);
  xor xor_4 (C24, inputA[24], inputB[24]);
  xor xor_5 (C22, inputA[22], inputB[22]);
  xor xor_6 (C20, inputA[20], inputB[20]);
  xor xor_7 (C18, inputA[18], inputB[18]);
  xor xor_8 (C16, inputA[16], inputB[16]);
  xor xor_9 (C14, inputA[14], inputB[14]);
  xor xor_10 (C12, inputA[12], inputB[12]);
  xor xor_11 (C10, inputA[10], inputB[10]);
  xor xor_12 (C08, inputA[8], inputB[8]);
  xor xor_13 (C06, inputA[6], inputB[6]);
  xor xor_14 (C04, inputA[4], inputB[4]);
  xor xor_15 (C02, inputA[2], inputB[2]);
  xor xor_16 (C00, inputA[0], inputB[0]);
  or or_1 (or_1_out, C30, C31, C28, C29, C26, C27, C24, C25, C22, C23, C20, C21, C18, C19, C16, C17, C15, C12, C13, C10, C11, C08, C09, C06, C07, C04, C05, C02, C03, C00, C01, C14);
  not not_1 (out_3, or_1_out);
  xor xor_17 (C31, inputA[31], inputB[31]);
  xor xor_18 (C29, inputA[29], inputB[29]);
  xor xor_19 (C27, inputA[27], inputB[27]);
  xor xor_20 (C25, inputA[25], inputB[25]);
  xor xor_21 (C23, inputA[23], inputB[23]);
  xor xor_22 (C21, inputA[21], inputB[21]);
  xor xor_23 (C19, inputA[19], inputB[19]);
  xor xor_24 (C17, inputA[17], inputB[17]);
  xor xor_25 (C15, inputA[15], inputB[15]);
  xor xor_26 (C13, inputA[13], inputB[13]);
  xor xor_27 (C11, inputA[11], inputB[11]);
  xor xor_28 (C09, inputA[9], inputB[9]);
  xor xor_29 (C07, inputA[7], inputB[7]);
  xor xor_30 (C05, inputA[5], inputB[5]);
  xor xor_31 (C03, inputA[3], inputB[3]);
  xor xor_32 (C01, inputA[1], inputB[1]);

  // Other names for the same wires on the sheet: A00 = inputA[0]; A01 = inputA[1]; A02 = inputA[2]; A03 = inputA[3];
  //   A04 = inputA[4]; A05 = inputA[5]; A06 = inputA[6]; A07 = inputA[7]; A08 = inputA[8]; A09 = inputA[9];
  //   A10 = inputA[10]; A11 = inputA[11]; A12 = inputA[12]; A13 = inputA[13]; A14 = inputA[14]; A15 = inputA[15];
  //   A16 = inputA[16]; A17 = inputA[17]; A18 = inputA[18]; A19 = inputA[19]; A20 = inputA[20]; A21 = inputA[21];
  //   A22 = inputA[22]; A23 = inputA[23]; A24 = inputA[24]; A25 = inputA[25]; A26 = inputA[26]; A27 = inputA[27];
  //   A28 = inputA[28]; A29 = inputA[29]; A30 = inputA[30]; A31 = inputA[31]; B00 = inputB[0]; B01 = inputB[1];
  //   B02 = inputB[2]; B03 = inputB[3]; B04 = inputB[4]; B05 = inputB[5]; B06 = inputB[6]; B07 = inputB[7];
  //   B08 = inputB[8]; B09 = inputB[9]; B10 = inputB[10]; B11 = inputB[11]; B12 = inputB[12]; B13 = inputB[13];
  //   B14 = inputB[14]; B15 = inputB[15]; B16 = inputB[16]; B17 = inputB[17]; B18 = inputB[18]; B19 = inputB[19];
  //   B20 = inputB[20]; B21 = inputB[21]; B22 = inputB[22]; B23 = inputB[23]; B24 = inputB[24]; B25 = inputB[25];
  //   B26 = inputB[26]; B27 = inputB[27]; B28 = inputB[28]; B29 = inputB[29]; B30 = inputB[30]; B31 = inputB[31]
endmodule
