// Logisim project COD4.3.2.circ as structural Verilog: 3 circuits, main circuit a
module a (
  input  A0,
  input  A1,
  output [7:0] out_3
);

  wire undriven;
  wire [7:0] _8Dflipflop_2_output, _8Dflipflop_3_output, _8Dflipflop_4_output, _8Dflipflop_output, and_1_out,
       and_2_out, and_3_out, and_4_out, and_5_out, and_6_out, bit_extender_1_out, bit_extender_2_out,
       not_1_out, not_2_out, not_3_out, or_1_out, or_2_out, undriven_2, undriven_3, undriven_4, undriven_5;

  _8bit_D_flip_flop _8Dflipflop (.Input(undriven_4), .clock(undriven), .Output(_8Dflipflop_output));  // open: Enable
  assign bit_extender_1_out = {{7{A0}}, A0};  // Bit_Extender bit_extender_1
  _8bit_D_flip_flop _8Dflipflop_2 (
    .Input(undriven_2), .clock(undriven), .Output(_8Dflipflop_2_output));  // open: Enable
  _8bit_D_flip_flop _8Dflipflop_3 (
    .Input(undriven_3), .clock(undriven), .Output(_8Dflipflop_3_output));  // open: Enable
  _8bit_D_flip_flop _8Dflipflop_4 (
    .Input(undriven_5), .clock(undriven), .Output(_8Dflipflop_4_output));  // open: Enable
  assign and_1_out = _8Dflipflop_2_output & bit_extender_1_out;  // AND_Gate and_1, 8 bits wide
  assign not_1_out = ~bit_extender_1_out;  // NOT_Gate not_1, 8 bits wide
  assign and_2_out = not_1_out & _8Dflipflop_3_output;  // AND_Gate and_2, 8 bits wide
  assign and_3_out = _8Dflipflop_output & bit_extender_1_out;  // AND_Gate and_3, 8 bits wide
  assign not_2_out = ~bit_extender_1_out;  // NOT_Gate not_2, 8 bits wide
  assign and_4_out = not_2_out & _8Dflipflop_4_output;  // AND_Gate and_4, 8 bits wide
  assign bit_extender_2_out = {{7{A1}}, A1};  // Bit_Extender bit_extender_2
  assign or_1_out = and_1_out | and_2_out;  // OR_Gate or_1, 8 bits wide
  assign or_2_out = and_3_out | and_4_out;  // OR_Gate or_2, 8 bits wide
  assign and_5_out = or_1_out & bit_extender_2_out;  // AND_Gate and_5, 8 bits wide
  assign not_3_out = ~bit_extender_2_out;  // NOT_Gate not_3, 8 bits wide
  assign and_6_out = not_3_out & or_2_out;  // AND_Gate and_6, 8 bits wide
  assign out_3 = and_5_out | and_6_out;  // OR_Gate or_3, 8 bits wide
endmodule

module _8bit_D_flip_flop (
  input  clock,
  input  [7:0] Input,
  input  Enable,
  output [7:0] Output
);

  wire undriven_2;
  wire [7:0] undriven;

  D_Flip_Flop d_ff_1 (.clk(undriven_2), .D(undriven[0]), .Q(Output[0]), .en(Enable));  // open: Qn, preset, reset
  D_Flip_Flop d_ff_2 (.clk(undriven_2), .D(undriven[1]), .Q(Output[1]), .en(Enable));  // open: Qn, preset, reset
  D_Flip_Flop d_ff_3 (.clk(undriven_2), .D(undriven[2]), .Q(Output[2]), .en(Enable));  // open: Qn, preset, reset
  D_Flip_Flop d_ff_4 (.clk(undriven_2), .D(undriven[3]), .Q(Output[3]), .en(Enable));  // open: Qn, preset, reset
  D_Flip_Flop d_ff_5 (.clk(undriven_2), .D(undriven[4]), .Q(Output[4]));  // open: Qn, preset, en, reset
  D_Flip_Flop d_ff_6 (.clk(undriven_2), .D(undriven[5]), .Q(Output[5]), .en(Enable));  // open: Qn, preset, reset
  D_Flip_Flop d_ff_7 (.clk(undriven_2), .D(undriven[6]), .Q(Output[6]), .en(Enable));  // open: Qn, preset, reset
  D_Flip_Flop d_ff_8 (.clk(undriven_2), .D(undriven[7]), .Q(Output[7]), .en(Enable));  // open: Qn, preset, reset
endmodule

module b (
  input  Read_register,
  input  [7:0] Write_Data,
  input  Write_register,
  input  RegWrite,
  output [7:0] Read_Data
);

  wire and_3_out, and_4_out, Clock_out, not_1_out;
  wire [7:0] and_1_out, and_2_out, bit_extender_1_out, n8bit_d_flip_flop_1_output,
       n8bit_d_flip_flop_2_output, not_2_out;

  Clock Clock (.out(Clock_out));
  assign bit_extender_1_out = {{7{Read_register}}, Read_register};  // Bit_Extender bit_extender_1
  _8bit_D_flip_flop u_8bit_d_flip_flop_1 (
    .Input(Write_Data), .clock(Clock_out), .Enable(and_4_out), .Output(n8bit_d_flip_flop_1_output));
  _8bit_D_flip_flop u_8bit_d_flip_flop_2 (
    .Input(Write_Data), .clock(Clock_out), .Enable(and_3_out), .Output(n8bit_d_flip_flop_2_output));
  not not_1 (not_1_out, Write_register);
  assign and_1_out = n8bit_d_flip_flop_1_output & bit_extender_1_out;  // AND_Gate and_1, 8 bits wide
  assign and_2_out = n8bit_d_flip_flop_2_output & not_2_out;  // AND_Gate and_2, 8 bits wide
  assign not_2_out = ~bit_extender_1_out;  // NOT_Gate not_2, 8 bits wide
  and and_3 (and_3_out, Write_register, RegWrite);
  and and_4 (and_4_out, not_1_out, RegWrite);
  assign Read_Data = and_1_out | and_2_out;  // OR_Gate or_1, 8 bits wide
endmodule
