// Logisim project GPR.circ as structural Verilog: 1 circuit, main circuit GPR
module GPR (
  input  clk,
  input  WE,
  input  reset,
  input  [4:0] A1,
  input  [4:0] A2,
  input  [4:0] A3,
  input  [31:0] WD,
  output [31:0] RD1,
  output [31:0] RD2
);

  wire R0WE, R1WE, R2WE, R3WE, R4WE, R5WE, R6WE, R7WE, R8WE, R9WE, R10WE, R11WE, R12WE, R13WE, R14WE, R15WE,
       R16WE, R17WE, R18WE, R19WE, R20WE, R21WE, R22WE, R23WE, R24WE, R25WE, R26WE, R27WE, R28WE, R29WE,
       R30WE, R31WE;
  wire [31:0] R0, R1, R2, R3, R4, R5, R6, R7, R8, R9, R10, R11, R12, R13, R14, R15, R16, R17, R18, R19, R20,
       R21, R22, R23, R24, R25, R26, R27, R28, R29, R30, R31;

  Register #(.width(32)) u_R12 (.D(WD), .en(R12WE), .Q(R12), .clk(clk), .clr(reset));
  Register #(.width(32)) u_R16 (.D(WD), .en(R16WE), .Q(R16), .clk(clk), .clr(reset));
  Register #(.width(32)) u_R20 (.D(WD), .en(R20WE), .Q(R20), .clk(clk), .clr(reset));
  Register #(.width(32)) u_R24 (.D(WD), .en(R24WE), .Q(R24), .clk(clk), .clr(reset));
  Register #(.width(32)) u_R28 (.D(WD), .en(R28WE), .Q(R28), .clk(clk), .clr(reset));
  Register #(.width(32)) u_R17 (.D(WD), .en(R17WE), .Q(R17), .clk(clk), .clr(reset));
  Register #(.width(32)) u_R21 (.D(WD), .en(R21WE), .Q(R21), .clk(clk), .clr(reset));
  Register #(.width(32)) u_R25 (.D(WD), .en(R25WE), .Q(R25), .clk(clk), .clr(reset));
  Register #(.width(32)) u_R29 (.D(WD), .en(R29WE), .Q(R29), .clk(clk), .clr(reset));
  Register #(.width(32)) u_R0 (.D(WD), .en(R0WE), .Q(R0), .clk(clk), .clr(reset));
  Register #(.width(32)) u_R4 (.D(WD), .en(R4WE), .Q(R4), .clk(clk), .clr(reset));
  Register #(.width(32)) u_R8 (.D(WD), .en(R8WE), .Q(R8), .clk(clk), .clr(reset));
  Register #(.width(32)) u_R13 (.D(WD), .en(R13WE), .Q(R13), .clk(clk), .clr(reset));
  Register #(.width(32)) u_R18 (.D(WD), .en(R18WE), .Q(R18), .clk(clk), .clr(reset));
  Register #(.width(32)) u_R1 (.D(WD), .en(R1WE), .Q(R1), .clk(clk), .clr(reset));
  Register #(.width(32)) u_R5 (.D(WD), .en(R5WE), .Q(R5), .clk(clk), .clr(reset));
  Register #(.width(32)) u_R9 (.D(WD), .en(R9WE), .Q(R9), .clk(clk), .clr(reset));
  Register #(.width(32)) u_R14 (.D(WD), .en(R14WE), .Q(R14), .clk(clk), .clr(reset));
  Register #(.width(32)) u_R22 (.D(WD), .en(R22WE), .Q(R22), .clk(clk), .clr(reset));
  Register #(.width(32)) u_R26 (.D(WD), .en(R26WE), .Q(R26), .clk(clk), .clr(reset));
  Register #(.width(32)) u_R30 (.D(WD), .en(R30WE), .Q(R30), .clk(clk), .clr(reset));
  Register #(.width(32)) u_R15 (.D(WD), .en(R15WE), .Q(R15), .clk(clk), .clr(reset));
  Register #(.width(32)) u_R19 (.D(WD), .en(R19WE), .Q(R19), .clk(clk), .clr(reset));
  Register #(.width(32)) u_R23 (.D(WD), .en(R23WE), .Q(R23), .clk(clk), .clr(reset));
  Register #(.width(32)) u_R27 (.D(WD), .en(R27WE), .Q(R27), .clk(clk), .clr(reset));
  Register #(.width(32)) u_R2 (.D(WD), .en(R2WE), .Q(R2), .clk(clk), .clr(reset));
  Register #(.width(32)) u_R6 (.D(WD), .en(R6WE), .Q(R6), .clk(clk), .clr(reset));
  Register #(.width(32)) u_R10 (.D(WD), .en(R10WE), .Q(R10), .clk(clk), .clr(reset));
  Register #(.width(32)) u_R31 (.D(WD), .en(R31WE), .Q(R31), .clk(clk), .clr(reset));
  Register #(.width(32)) u_R3 (.D(WD), .en(R3WE), .Q(R3), .clk(clk), .clr(reset));
  Register #(.width(32)) u_R7 (.D(WD), .en(R7WE), .Q(R7), .clk(clk), .clr(reset));
  Register #(.width(32)) u_R11 (.D(WD), .en(R11WE), .Q(R11), .clk(clk), .clr(reset));
  Decoder #(.select(5), .disabled(0)) decoder_1 (
    .out0(R0WE), .out1(R1WE), .out2(R2WE), .out3(R3WE), .out4(R4WE), .out5(R5WE), .out6(R6WE), .out7(R7WE),
    .out8(R8WE), .out9(R9WE), .out10(R10WE), .out11(R11WE), .out12(R12WE), .out13(R13WE), .out14(R14WE),
    .out15(R15WE), .out16(R16WE), .out17(R17WE), .out18(R18WE), .out19(R19WE), .out20(R20WE), .out21(R21WE),
    .out22(R22WE), .out23(R23WE), .out24(R24WE), .out25(R25WE), .out26(R26WE), .out27(R27WE), .out28(R28WE),
    .out29(R29WE), .out30(R30WE), .out31(R31WE), .sel(A3), .en(WE));
  Multiplexer #(.select(5), .width(32), .enable("false")) multiplexer_1 (
    .in0(R0), .in1(R1), .in2(R2), .in3(R3), .in4(R4), .in5(R5), .in6(R6), .in7(R7), .in8(R8), .in9(R9),
    .in10(R10), .in11(R11), .in12(R12), .in13(R13), .in14(R14), .in15(R15), .in16(R16), .in17(R17),
    .in18(R18), .in19(R19), .in20(R20), .in21(R21), .in22(R22), .in23(R23), .in24(R24), .in25(R25),
    .in26(R26), .in27(R27), .in28(R28), .in29(R29), .in30(R30), .in31(R31), .out(RD1), .sel(A1));
  Multiplexer #(.select(5), .width(32), .enable("false")) multiplexer_2 (
    .in0(R0), .in1(R1), .in2(R2), .in3(R3), .in4(R4), .in5(R5), .in6(R6), .in7(R7), .in8(R8), .in9(R9),
    .in10(R10), .in11(R11), .in12(R12), .in13(R13), .in14(R14), .in15(R15), .in16(R16), .in17(R17),
    .in18(R18), .in19(R19), .in20(R20), .in21(R21), .in22(R22), .in23(R23), .in24(R24), .in25(R25),
    .in26(R26), .in27(R27), .in28(R28), .in29(R29), .in30(R30), .in31(R31), .out(RD2), .sel(A2));
endmodule
