// Logisim project Transistor Gates 1.60.circ as structural Verilog: 3 circuits, main circuit A four-input NAND gate
module A_four_input_NAND_gate (
  input  A,
  input  B,
  input  C,
  input  D,
  output Y
);

  wire transistor_6_out, transistor_7_out, transistor_8_out;

  Transistor transistor_1 (.in(1'b1), .out(Y), .gate(B));
  Transistor transistor_2 (.in(1'b1), .out(Y), .gate(A));
  Transistor transistor_3 (.in(1'b1), .out(Y), .gate(D));
  Transistor transistor_4 (.in(1'b1), .out(Y), .gate(C));
  Transistor #(.\type ("n")) transistor_5 (.in(transistor_6_out), .out(Y), .gate(D));
  Transistor #(.\type ("n")) transistor_6 (.in(transistor_7_out), .out(transistor_6_out), .gate(C));
  Transistor #(.\type ("n")) transistor_7 (.in(transistor_8_out), .out(transistor_7_out), .gate(B));
  Transistor #(.\type ("n")) transistor_8 (.in(1'b0), .out(transistor_8_out), .gate(A));
endmodule

module A_three_input_OR_AND_INVERT_gate (
  input  A,
  input  B,
  input  C,
  output Y
);

  wire transistor_1_out, transistor_2_out, transistor_5_out, transistor_10_out;

  Transistor transistor_1 (.in(1'b1), .out(transistor_1_out), .gate(A));
  Transistor transistor_2 (.in(transistor_1_out), .out(transistor_2_out), .gate(B));
  Transistor #(.\type ("n")) transistor_3 (.in(1'b0), .out(transistor_2_out), .gate(B));
  Transistor #(.\type ("n")) transistor_4 (.in(1'b0), .out(transistor_2_out), .gate(A));
  Transistor transistor_5 (.in(1'b1), .out(transistor_5_out), .gate(transistor_2_out));
  Transistor #(.\type ("n")) transistor_6 (.in(1'b0), .out(transistor_5_out), .gate(transistor_2_out));
  Transistor transistor_7 (.in(1'b1), .out(Y), .gate(C));
  Transistor transistor_8 (.in(1'b1), .out(Y), .gate(transistor_5_out));
  Transistor #(.\type ("n")) transistor_9 (.in(transistor_10_out), .out(Y), .gate(transistor_5_out));
  Transistor #(.\type ("n")) transistor_10 (.in(1'b0), .out(transistor_10_out), .gate(C));
endmodule

module A_three_input_AND_OR_gate (
  input  A,
  input  B,
  input  C,
  output Y
);

  wire transistor_1_out, transistor_4_out, transistor_5_out, transistor_7_out, transistor_8_out;

  Transistor transistor_1 (.in(1'b1), .out(transistor_1_out), .gate(A));
  Transistor transistor_2 (.in(1'b1), .out(transistor_1_out), .gate(B));
  Transistor #(.\type ("n")) transistor_3 (.in(transistor_4_out), .out(transistor_1_out), .gate(A));
  Transistor #(.\type ("n")) transistor_4 (.in(1'b0), .out(transistor_4_out), .gate(B));
  Transistor transistor_5 (.in(1'b1), .out(transistor_5_out), .gate(transistor_1_out));
  Transistor #(.\type ("n")) transistor_6 (.in(1'b0), .out(transistor_5_out), .gate(transistor_1_out));
  Transistor transistor_7 (.in(1'b1), .out(transistor_7_out), .gate(transistor_5_out));
  Transistor transistor_8 (.in(transistor_7_out), .out(transistor_8_out), .gate(C));
  Transistor #(.\type ("n")) transistor_9 (.in(1'b0), .out(transistor_8_out), .gate(transistor_5_out));
  Transistor #(.\type ("n")) transistor_10 (.in(1'b0), .out(transistor_8_out), .gate(C));
  Transistor transistor_11 (.in(1'b1), .out(Y), .gate(transistor_8_out));
  Transistor #(.\type ("n")) transistor_12 (.in(1'b0), .out(Y), .gate(transistor_8_out));
endmodule
