// Logisim project Xor.circ as structural Verilog: 2 circuits, main circuit main
module main (
  input  x,
  input  y,
  input  in_3,
  input  in_4,
  input  in_5,
  input  in_6,
  input  in_7,
  input  in_8,
  output out_9,
  output out_10
);

  wire and_1_out, and_2_out, hello_1_out, hello_3_out, not_1_out, not_2_out;

  // Probe on not_1_out
  not not_1 (not_1_out, x);
  not not_2 (not_2_out, y);
  and and_1 (and_1_out, not_1_out, y);
  and and_2 (and_2_out, x, not_2_out);
  hello hello_1 (.in_0(in_3), .in_1(in_5), .out(hello_1_out), .select(in_8));
  hello hello_2 (.in_0(hello_1_out), .in_1(hello_3_out), .out(out_10), .select(in_4));
  hello hello_3 (.in_0(in_6), .in_1(in_7), .out(hello_3_out), .select(in_8));
  or or_1 (out_9, and_1_out, and_2_out);

  // Notes on the sheet:
  //   Xor Circuit
endmodule

module hello (
  input  in_0,
  input  in_1,
  input  select,
  output out
);

  wire and_1_out, and_2_out, not_1_out;

  not not_1 (not_1_out, select);
  and and_1 (and_1_out, in_0, not_1_out);
  and and_2 (and_2_out, select, in_1);
  or or_1 (out, and_1_out, and_2_out);
endmodule
