// Logisim project adder.circ as structural Verilog: 2 circuits, main circuit full adder
module full_adder (
  input  A,
  input  B,
  input  C1,
  output S,
  output C2
);

  wire and_1_out, and_2_out, and_3_out, xor_1_out;

  xor xor_1 (xor_1_out, A, B);
  and and_1 (and_1_out, A, B);
  and and_2 (and_2_out, C1, A);
  and and_3 (and_3_out, B, C1);
  xor xor_2 (S, xor_1_out, C1);
  or or_1 (C2, and_1_out, and_2_out, and_3_out);
endmodule

module four_bit_adder (
  input  in_1,
  input  in_2,
  input  in_3,
  input  in_4,
  input  in_5,
  input  in_6,
  input  in_7,
  input  in_8,
  input  in_9,
  output out_10,
  output out_11,
  output out_12,
  output out_13,
  output out_14
);

  wire full_adder_1_c2, full_adder_2_c2, full_adder_3_c2;

  full_adder full_adder_1 (.A(in_1), .B(in_6), .C1(in_5), .S(out_10), .C2(full_adder_1_c2));
  full_adder full_adder_2 (.A(in_2), .B(in_7), .C1(full_adder_1_c2), .S(out_11), .C2(full_adder_2_c2));
  full_adder full_adder_3 (.A(in_3), .B(in_8), .C1(full_adder_2_c2), .S(out_12), .C2(full_adder_3_c2));
  full_adder full_adder_4 (.A(in_4), .B(in_9), .C1(full_adder_3_c2), .S(out_13), .C2(out_14));
endmodule
