// Logisim project loopAdderMachine.circ as structural Verilog: 2 circuits, main circuit addMachine
module addMachine (
  output [15:0] S
);

  wire clock_1_out;
  wire [15:0] register_1_q;

  Adder #(.width(16)) adder_1 (.a(16'h1), .b(register_1_q), .out(S));  // open: cin, cout
  Clock clock_1 (.out(clock_1_out));
  Register #(.width(16)) register_1 (.D(S), .Q(register_1_q), .clk(clock_1_out));  // open: en, clr
  // Probe on register_1_q
endmodule

module realmain (
  output [15:0] out_1,
  output [15:0] out_2
);

  addMachine addmachine_1 (.S(out_1));
  addMachine addmachine_2 (.S(out_2));
endmodule
