// Logisim project project1-adder.circ as structural Verilog: 3 circuits, main circuit 8bit-adder
module _8bit_adder (
  input  [7:0] inputA,
  input  [7:0] inputB,
  input  Cin,
  output Cout,
  output [7:0] \output 
);

  wire n4_bit_adder_2_c4;

  _4_bit_adder u_4_bit_adder_1 (
    .c4(Cout), .C0(n4_bit_adder_2_c4), .A3(inputB[7]), .B3(inputA[7]), .A2(inputB[6]), .B2(inputA[6]),
    .A1(inputB[5]), .B1(inputA[5]), .A0(inputB[4]), .B0(inputA[4]), .S3(\output [7]), .S2(\output [6]),
    .S1(\output [5]), .S0(\output [4]));
  _4_bit_adder u_4_bit_adder_2 (
    .c4(n4_bit_adder_2_c4), .C0(Cin), .A3(inputB[3]), .B3(inputA[3]), .A2(inputB[2]), .B2(inputA[2]),
    .A1(inputB[1]), .B1(inputA[1]), .A0(inputB[0]), .B0(inputA[0]), .S3(\output [3]), .S2(\output [2]),
    .S1(\output [1]), .S0(\output [0]));
endmodule

module one_bit_adder (
  input  A,
  input  B,
  input  Cin,
  output S,
  output Cout
);

  wire and_1_out, and_2_out, xor_1_out;

  xor xor_1 (xor_1_out, A, B);
  and and_1 (and_1_out, xor_1_out, Cin);
  and and_2 (and_2_out, A, B);
  xor xor_2 (S, xor_1_out, Cin);
  or or_1 (Cout, and_1_out, and_2_out);
endmodule

module _4_bit_adder (
  input  A3,
  input  B3,
  input  A2,
  input  B2,
  input  A1,
  input  B1,
  input  A0,
  input  B0,
  input  C0,
  output c4,
  output S3,
  output S2,
  output S1,
  output S0
);

  wire one_bit_adder_2_cout, one_bit_adder_3_cout, one_bit_adder_4_cout;

  one_bit_adder one_bit_adder_1 (.A(A3), .B(B3), .Cin(one_bit_adder_2_cout), .S(S3), .Cout(c4));
  one_bit_adder one_bit_adder_2 (.A(A2), .B(B2), .Cin(one_bit_adder_3_cout), .S(S2), .Cout(one_bit_adder_2_cout));
  one_bit_adder one_bit_adder_3 (.A(A1), .B(B1), .Cin(one_bit_adder_4_cout), .S(S1), .Cout(one_bit_adder_3_cout));
  one_bit_adder one_bit_adder_4 (.A(A0), .B(B0), .Cin(C0), .S(S0), .Cout(one_bit_adder_4_cout));

  // Notes on the sheet:
  //   C3
  //   c2
  //   c1
endmodule
