// Logisim project mips-lite-single-cycle.circ as structural Verilog: 4 circuits, main circuit main
module main (
  input  reset
);

  wire alu_1_p4, ALUSrc, clock_1_out, ExtOp, Mem2reg, MemWrite, nPC_sel, RegDst, RegWrite;
  wire [1:0] ALUOp_1_0;
  wire [4:0] multiplexer_1_out, rs, rt;
  wire [5:0] funct, op;
  wire [15:6] imm;
  wire [31:0] alu_1_p2, ALUresult, extender_1_output, multiplexer_2_out, ram_1_data, RD1, RD2;

  Controller controller_1 (
    .opCode_5_0(op), .funct_5_0(funct), .RegDst(RegDst), .ALUSrc(ALUSrc), .Mem2Reg(Mem2reg),
    .RegWrite(RegWrite), .MemWrite(MemWrite), .nPC_sel(nPC_sel), .ExtOp(ExtOp), .ALUOp_1_0(ALUOp_1_0));
  Clock clock_1 (.out(clock_1_out));
  IFU ifu_1 (.IfBeq(nPC_sel), .clk(clock_1_out), .Zero(alu_1_p4), .Instr({op, rs, rt, imm, funct}), .reset(reset));
  Multiplexer #(.width(5), .enable("false")) multiplexer_1 (
    .in0(rt), .in1(imm[15:11]), .out(multiplexer_1_out), .sel(RegDst));
  Multiplexer #(.width(32), .enable("false")) multiplexer_2 (
    .in0(ALUresult), .in1(ram_1_data), .out(multiplexer_2_out), .sel(Mem2reg));
  // Probe on op
  // Probe on rs
  // Probe on rt
  // Probe on imm[15:11]
  GPR gpr_1 (
    .reset(reset), .A1(rs), .A2(rt), .A3(multiplexer_1_out), .WD(multiplexer_2_out), .RD1(RD1), .RD2(RD2),
    .WE(RegWrite), .clk(clock_1_out));
  Extender extender_1 (.\input ({imm, funct}), .\output (extender_1_output), .ExtOp(ExtOp));
  // ALU alu_1: pin names not known; wires that end beside it: RD1, alu_1_p2, ALUOp_1_0, alu_1_p4, ALUresult
  Multiplexer #(.width(32), .enable("false")) multiplexer_3 (
    .in0(RD2), .in1(extender_1_output), .out(alu_1_p2), .sel(ALUSrc));
  RAM #(.addrWidth(5), .dataWidth(32), .bus("separate")) ram_1 (
    .addr(ALUresult[6:2]), .din(RD2), .data(ram_1_data), .str(MemWrite), .clk(clock_1_out));  // open: sel, ld, clr

  // Other names for the same wires on the sheet: imm[5:0] = funct; rd[4:0] = imm[15:11]
endmodule

module Controller (
  input  [5:0] opCode_5_0,
  input  [5:0] funct_5_0,
  output RegDst,
  output ALUSrc,
  output Mem2Reg,
  output RegWrite,
  output MemWrite,
  output nPC_sel,
  output ExtOp,
  output [1:0] ALUOp_1_0
);

  wire add_out, not_1_out, not_2_out, not_3_out, not_4_out, not_5_out, not_6_out, not_7_out, not_8_out,
       not_9_out, not_10_out, not_11_out, not_12_out, R_type_out, sub_out;

  not not_1 (not_1_out, opCode_5_0[5]);
  not not_2 (not_2_out, opCode_5_0[4]);
  not not_3 (not_3_out, opCode_5_0[3]);
  not not_4 (not_4_out, opCode_5_0[2]);
  not not_5 (not_5_out, opCode_5_0[1]);
  not not_6 (not_6_out, opCode_5_0[0]);
  not not_7 (not_7_out, funct_5_0[5]);
  and R_type (R_type_out, not_1_out, not_2_out, not_3_out, not_4_out, not_5_out, not_6_out);
  and ori (ALUOp_1_0[1], not_1_out, not_2_out, opCode_5_0[3], opCode_5_0[2], not_5_out, opCode_5_0[0]);
  and lw (Mem2Reg, opCode_5_0[5], not_2_out, not_3_out, not_4_out, opCode_5_0[1], opCode_5_0[0]);
  and sw (MemWrite, opCode_5_0[5], not_2_out, opCode_5_0[3], not_4_out, opCode_5_0[1], opCode_5_0[0]);
  and beq (nPC_sel, not_1_out, not_2_out, not_3_out, opCode_5_0[2], not_5_out, not_6_out);
  not not_8 (not_8_out, funct_5_0[4]);
  not not_9 (not_9_out, funct_5_0[3]);
  not not_10 (not_10_out, funct_5_0[2]);
  not not_11 (not_11_out, funct_5_0[1]);
  not not_12 (not_12_out, funct_5_0[0]);
  or or_1 (RegDst, sub_out, add_out);
  and add (add_out, R_type_out, funct_5_0[5], not_8_out, not_9_out, not_10_out, not_11_out, not_12_out);
  and sub (sub_out, R_type_out, funct_5_0[5], not_8_out, not_9_out, not_10_out, funct_5_0[1], not_12_out);
  or or_2 (ALUSrc, MemWrite, Mem2Reg, ALUOp_1_0[1]);
  or or_3 (RegWrite, add_out, sub_out, ALUOp_1_0[1], Mem2Reg);
  or or_4 (ExtOp, MemWrite, Mem2Reg);
  or or_5 (ALUOp_1_0[0], nPC_sel, sub_out);
endmodule

module IFU (
  input  IfBeq,
  input  reset,
  input  clk,
  input  Zero,
  output [31:0] Instr
);

  wire and_1_out;
  wire [29:0] currentPC30;
  wire [31:0] bit_extender_1_out, bit_extender_2_out, multiplexer_1_out, n32bit_adder_1_result,
       n32bit_adder_2_result;

  assign bit_extender_1_out = {{2{currentPC30[29]}}, currentPC30};  // Bit_Extender bit_extender_1
  assign bit_extender_2_out = {{16{Instr[15]}}, Instr[15:0]};  // Bit_Extender bit_extender_2
  _32bit_adder u_32bit_adder_1 (.inputA(bit_extender_1_out), .inputB(32'h1), .result(n32bit_adder_1_result));
  _32bit_adder u_32bit_adder_2 (
    .inputA(bit_extender_2_out), .inputB(n32bit_adder_1_result), .result(n32bit_adder_2_result));
  and and_1 (and_1_out, IfBeq, Zero);
  Multiplexer #(.width(32), .enable("false")) multiplexer_1 (
    .in0(n32bit_adder_1_result), .in1(n32bit_adder_2_result), .out(multiplexer_1_out), .sel(and_1_out));
  Register #(.width(30)) PC (.D(multiplexer_1_out[29:0]), .Q(currentPC30), .clk(clk), .clr(reset));  // open: en
  ROM #(.addrWidth(5), .dataWidth(32)) rom_1 (.addr(currentPC30[4:0]), .data(Instr));  // open: sel

  // Other names for the same wires on the sheet: currentInstr_15_0[15:0] = Instr[15:0]

  // Notes on the sheet:
  //   contents of rom_1 (hex, n*v repeats v):
  //   8c1f0000 8c1e0004 3dfe820 3dfe022 ac1d0008 ac1c000c 8c010010 3422aaaa ac020014 8c030018 8c040018
  //   10640001 ac030020 641820 8c05001c 1065fffb
endmodule

module Extender (
  input  [15:0] \input ,
  input  ExtOp,
  output [31:0] \output 
);

  wire [31:0] bit_extender_1_out, bit_extender_2_out;

  assign bit_extender_1_out = {{16{1'b0}}, \input };  // Bit_Extender bit_extender_1
  assign bit_extender_2_out = {{16{\input [15]}}, \input };  // Bit_Extender bit_extender_2
  Multiplexer #(.width(32), .enable("false")) multiplexer_1 (
    .in0(bit_extender_1_out), .in1(bit_extender_2_out), .out(\output ), .sel(ExtOp));
endmodule
