// Logisim project mips-lite2-pipeline.circ as structural Verilog: 10 circuits, main circuit main
module main (
  input  reset
);

  wire ALUSrc, and_1_out, clk, Contr_nen, ex_mem_1_out_13, FWD_M, id_ex_1_out_17, id_ex_1_out_19,
       IF_Flush_out, MemWrite, not_1_out, nPC_sel, or_1_out, RegW_E, RegWrite, RegWriteW, RW_M, zero;
  wire [1:0] ALUOp_1_0, ExtOp, FA_D, FA_E, FB_D, FB_E, id_ex_1_out_22, IfJ, Mem2reg, mem_wb_1_out_11, MemR_E,
       MTR_M, RegD_E, RegDst;
  wire [4:0] ex_mem_1_out_18, ex_mem_1_out_19, id_ex_1_out_27, id_ex_1_out_28, id_ex_1_out_29,
       multiplexer_4_out, rs, rt, WriteRegW;
  wire [5:0] funct, op;
  wire [8:0] and_2_out, bit_extender_1_out, not_2_out;
  wire [15:6] imm;
  wire [31:0] alu_1_result, ALUresultM, ex_mem_1_out_15, ex_mem_1_out_17, extender_1_output, gpr_1_rd1,
       gpr_1_rd2, id_ex_1_out_23, id_ex_1_out_24, id_ex_1_out_25, id_ex_1_out_26, IDRD1, IDRD2,
       ifu_1_curinstr, mem_wb_1_out_12, mem_wb_1_out_13, mem_wb_1_out_14, multiplexer_1_out,
       multiplexer_5_out, multiplexer_6_out, multiplexer_7_out, multiplexer_8_out, n32bit_adder_1_result, PC,
       PC_4, ram_1_data, subtractor_1_out, WRD_W;

  IFU ifu_1 (
    .IfBeq(nPC_sel), .clk(clk), .Zero(zero), .CurInstr(ifu_1_curinstr), .reset(reset), .rs(IDRD1), .IfJ(IfJ),
    .nen(Contr_nen), .currentPC(PC));
  _32bit_adder u_32bit_adder_1 (.inputA(PC), .inputB(32'h4), .result(n32bit_adder_1_result));
  // Probe on PC
  and and_1 (and_1_out, nPC_sel, zero);
  Multiplexer #(.width(32), .enable("false")) multiplexer_1 (
    .in0(ifu_1_curinstr), .in1({32{1'b0}}), .out(multiplexer_1_out), .sel(IF_Flush_out));
  not not_1 (not_1_out, Contr_nen);
  or IF_Flush (IF_Flush_out, and_1_out, or_1_out);
  or or_1 (or_1_out, IfJ[1], IfJ[0]);
  Register #(.width(32)) u_PC_4 (.D(n32bit_adder_1_result), .en(not_1_out), .Q(PC_4), .clk(clk), .clr(reset));
  Register #(.width(32)) Instr (
    .D(multiplexer_1_out), .en(not_1_out), .Q({op, rs, rt, imm, funct}), .clk(clk), .clr(reset));
  Controller controller_1 (
    .opCode_5_0(op), .funct_5_0(funct), .RegDst(RegDst), .ALUSrc(ALUSrc), .Mem2Reg(Mem2reg),
    .RegWrite(RegWrite), .MemWrite(MemWrite), .nPC_sel(nPC_sel), .ExtOp(ExtOp), .ALUOp_1_0(ALUOp_1_0),
    .IfJ(IfJ));
  GPR gpr_1 (
    .reset(reset), .A1(rs), .A2(rt), .A3(WriteRegW), .WD(WRD_W), .RD1(gpr_1_rd1), .RD2(gpr_1_rd2),
    .WE(RegWriteW), .clk(clk));
  // Probe on op
  // Probe on rs
  // Probe on rt
  // Probe on imm[15:11]
  // Probe on funct
  assign bit_extender_1_out = {{8{Contr_nen}}, Contr_nen};  // Bit_Extender bit_extender_1
  Subtractor #(.width(32)) subtractor_1 (.a(IDRD1), .b(IDRD2), .out(subtractor_1_out));  // open: bin, bout
  Comparator #(.width(32)) comparator_1 (.a(subtractor_1_out), .b({32{1'b0}}), .eq(zero));  // open: gt, lt
  Multiplexer #(.select(2), .width(32), .enable("false")) multiplexer_2 (
    .in0(gpr_1_rd1), .in1(ALUresultM), .in2(WRD_W), .out(IDRD1), .sel(FA_D));  // open: in3
  Multiplexer #(.select(2), .width(32), .enable("false")) multiplexer_3 (
    .in0(gpr_1_rd2), .in1(ALUresultM), .in2(WRD_W), .out(IDRD2), .sel(FB_D));  // open: in3
  assign and_2_out = {ALUOp_1_0, RegDst, Mem2reg, MemWrite, RegWrite, ALUSrc} & not_2_out;  // AND_Gate and_2, 9 bits wide
  assign not_2_out = ~bit_extender_1_out;  // NOT_Gate not_2, 9 bits wide
  Extender extender_1 (.\input ({imm, funct}), .\output (extender_1_output), .ExtOp(ExtOp));
  ID_EX id_ex_1 (
    .in_1(and_2_out[0]), .in_2(and_2_out[1]), .in_3(and_2_out[2]), .in_4(and_2_out[4:3]),
    .in_5(and_2_out[6:5]), .in_6(and_2_out[8:7]), .in_7(PC_4), .in_8(IDRD1), .in_9(IDRD2),
    .in_10(extender_1_output), .in_11(rs), .in_12(rt), .in_13(imm[15:11]), .out_17(id_ex_1_out_17),
    .out_18(RegW_E), .out_19(id_ex_1_out_19), .out_20(MemR_E), .out_21(RegD_E), .out_22(id_ex_1_out_22),
    .out_23(id_ex_1_out_23), .out_24(id_ex_1_out_24), .out_25(id_ex_1_out_25), .out_26(id_ex_1_out_26),
    .out_27(id_ex_1_out_27), .out_28(id_ex_1_out_28), .out_29(id_ex_1_out_29), .clk(clk), .reset(reset));  // open: nen
  Clock clock_1 (.out(clk));
  Multiplexer #(.select(2), .width(5), .enable("false")) multiplexer_4 (
    .in0(id_ex_1_out_28), .in1(id_ex_1_out_29), .in2({5{1'b1}}), .out(multiplexer_4_out), .sel(RegD_E));  // open: in3
  Stall_Unit stall_unit_1 (
    .ID_rs(rs), .ID_rt(rt), .ID_EX_MemReg(MemR_E), .ID_EX_rt(id_ex_1_out_28), .ID_EX_rd(id_ex_1_out_29),
    .ID_EX_RegDst(RegD_E), .EX_Mem_WriteReg(ex_mem_1_out_19), .beq(nPC_sel), .ID_EX_RegWrite(RegW_E),
    .IfJ(IfJ), .EX_Mem_MemReg(MTR_M), .stall(Contr_nen));
  Multiplexer #(.select(2), .width(32), .enable("false")) multiplexer_5 (
    .in0(id_ex_1_out_24), .in1(ALUresultM), .in2(WRD_W), .out(multiplexer_5_out), .sel(FA_E));  // open: in3
  Multiplexer #(.select(2), .width(32), .enable("false")) multiplexer_6 (
    .in0(id_ex_1_out_25), .in1(ALUresultM), .in2(WRD_W), .out(multiplexer_6_out), .sel(FB_E));  // open: in3
  ALU alu_1 (
    .inputA(multiplexer_5_out), .inputB(multiplexer_7_out), .result(alu_1_result), .ALUOp_1_0(id_ex_1_out_22));  // open: zero
  Multiplexer #(.width(32), .enable("false")) multiplexer_7 (
    .in0(multiplexer_6_out), .in1(id_ex_1_out_26), .out(multiplexer_7_out), .sel(id_ex_1_out_17));
  EX_MEM ex_mem_1 (
    .in_1(RegW_E), .in_2(id_ex_1_out_19), .in_3(MemR_E), .in_4(id_ex_1_out_23), .in_5(alu_1_result),
    .in_6(multiplexer_6_out), .in_7(id_ex_1_out_28), .out_12(RW_M), .out_13(ex_mem_1_out_13), .out_14(MTR_M),
    .out_15(ex_mem_1_out_15), .out_16(ALUresultM), .out_17(ex_mem_1_out_17), .out_18(ex_mem_1_out_18),
    .clk(clk), .reset(reset), .in_8(multiplexer_4_out), .out_19(ex_mem_1_out_19));  // open: nen
  Multiplexer #(.width(32), .enable("false")) multiplexer_8 (
    .in0(ex_mem_1_out_17), .in1(WRD_W), .out(multiplexer_8_out), .sel(FWD_M));
  Forward_Unit forward_unit_1 (
    .ID_EX_rs(id_ex_1_out_27), .ID_EX_rt(id_ex_1_out_28), .Ex_MEM_WriteReg(ex_mem_1_out_19),
    .RegWriteM(RW_M), .Mem2RegM(MTR_M), .MEM_WB_WriteReg(WriteRegW), .RegWriteWB(RegWriteW),
    .Ex_MEM_rt(ex_mem_1_out_18), .MemWriteM(ex_mem_1_out_13), .beq(nPC_sel), .IfJ(IfJ), .ID_rs(rs),
    .ID_rt(rt), .FowardAE(FA_E), .FowardBE(FB_E), .FowardWData_M(FWD_M), .FowardAD(FA_D), .FowardBD(FB_D));
  MEM_WB mem_wb_1 (
    .in_1(RW_M), .in_2(MTR_M), .in_3(ex_mem_1_out_15), .in_4(ram_1_data), .in_5(ALUresultM),
    .in_6(ex_mem_1_out_19), .out_10(RegWriteW), .out_11(mem_wb_1_out_11), .out_12(mem_wb_1_out_12),
    .out_13(mem_wb_1_out_13), .out_14(mem_wb_1_out_14), .out_15(WriteRegW), .clk(clk), .reset(reset));  // open: nen
  RAM #(.addrWidth(10), .dataWidth(32), .bus("separate")) ram_1 (
    .addr(ALUresultM[11:2]), .din(multiplexer_8_out), .data(ram_1_data), .str(ex_mem_1_out_13), .clk(clk),
    .ld(1'b1));  // open: sel, clr
  Multiplexer #(.select(2), .width(32), .enable("false")) multiplexer_9 (
    .in0(mem_wb_1_out_14), .in1(mem_wb_1_out_13), .in2(mem_wb_1_out_12), .out(WRD_W), .sel(mem_wb_1_out_11));  // open: in3

  // Other names for the same wires on the sheet: imm[5:0] = funct; rd[4:0] = imm[15:11]; IF_ID_nen = Contr_nen;
  //   PC_nen = Contr_nen

  // Notes on the sheet:
  //   IF/ID
  //   Entrance
endmodule

module Controller (
  input  [5:0] funct_5_0,
  input  [5:0] opCode_5_0,
  output [1:0] RegDst,
  output ALUSrc,
  output [1:0] Mem2Reg,
  output RegWrite,
  output MemWrite,
  output nPC_sel,
  output [1:0] ExtOp,
  output [1:0] ALUOp_1_0,
  output [1:0] IfJ
);

  wire add_out, j_out, jr_out, not_1_out, not_2_out, not_3_out, not_4_out, not_5_out, not_6_out, not_7_out,
       not_8_out, not_9_out, not_10_out, not_11_out, not_12_out, ori_out, R_type_out, sub_out;

  not not_1 (not_1_out, opCode_5_0[5]);
  not not_2 (not_2_out, opCode_5_0[4]);
  not not_3 (not_3_out, opCode_5_0[3]);
  not not_4 (not_4_out, opCode_5_0[2]);
  not not_5 (not_5_out, opCode_5_0[1]);
  not not_6 (not_6_out, opCode_5_0[0]);
  and jr (jr_out, not_7_out, not_8_out, funct_5_0[3], R_type_out, not_10_out, not_11_out, not_12_out);
  not not_7 (not_7_out, funct_5_0[5]);
  and R_type (R_type_out, not_1_out, not_2_out, not_3_out, not_4_out, not_5_out, not_6_out);
  and ori (ori_out, not_1_out, not_2_out, opCode_5_0[3], opCode_5_0[2], not_5_out, opCode_5_0[0]);
  and lw (Mem2Reg[0], opCode_5_0[5], not_2_out, not_3_out, not_4_out, opCode_5_0[1], opCode_5_0[0]);
  and sw (MemWrite, opCode_5_0[5], not_2_out, opCode_5_0[3], not_4_out, opCode_5_0[1], opCode_5_0[0]);
  and beq (nPC_sel, not_1_out, not_2_out, not_3_out, opCode_5_0[2], not_5_out, not_6_out);
  and j (j_out, not_1_out, not_2_out, not_3_out, not_4_out, opCode_5_0[1], not_6_out);
  and jal (Mem2Reg[1], not_1_out, not_2_out, not_3_out, not_4_out, opCode_5_0[1], opCode_5_0[0]);
  and lui (ExtOp[1], not_1_out, not_2_out, opCode_5_0[3], opCode_5_0[2], opCode_5_0[1], opCode_5_0[0]);
  not not_8 (not_8_out, funct_5_0[4]);
  not not_9 (not_9_out, funct_5_0[3]);
  or or_1 (IfJ[1], j_out, Mem2Reg[1]);
  not not_10 (not_10_out, funct_5_0[2]);
  not not_11 (not_11_out, funct_5_0[1]);
  not not_12 (not_12_out, funct_5_0[0]);
  or or_2 (RegDst[0], sub_out, add_out);
  or or_3 (IfJ[0], jr_out, Mem2Reg[1]);
  and add (add_out, R_type_out, funct_5_0[5], not_8_out, not_9_out, not_10_out, not_11_out, funct_5_0[0]);
  and sub (sub_out, R_type_out, funct_5_0[5], not_8_out, not_9_out, not_10_out, funct_5_0[1], funct_5_0[0]);
  or or_4 (ALUSrc, MemWrite, Mem2Reg[0], ori_out);
  or or_5 (RegWrite, add_out, sub_out, Mem2Reg[1], ori_out, Mem2Reg[0]);
  or or_6 (ALUOp_1_0[1], ExtOp[1], ori_out);
  or or_7 (ExtOp[0], MemWrite, Mem2Reg[0]);
  or or_8 (ALUOp_1_0[0], nPC_sel, ExtOp[1], sub_out);

  assign RegDst[1] = Mem2Reg[1];
endmodule

module IFU (
  input  [31:0] rs,
  input  [1:0] IfJ,
  input  IfBeq,
  input  Zero,
  input  nen,
  input  clk,
  input  reset,
  output [31:0] currentPC,
  output [31:0] CurInstr
);

  wire and_1_out, and_2_out, not_1_out, not_2_out;
  wire [1:0] or_2_out, undriven;
  wire [15:0] currentInstr_15_0;
  wire [31:0] bit_extender_1_out, bit_extender_2_out, bit_extender_3_out, multiplexer_1_out,
       n32bit_adder_1_result, n32bit_adder_2_result;
  wire [31:16] LastInstr;

  assign bit_extender_1_out = {{2{currentPC[31]}}, currentPC[31:2]};  // Bit_Extender bit_extender_1
  assign bit_extender_2_out = {{2{1'b0}}, {currentPC[31:28], LastInstr[25:16], currentInstr_15_0}};  // Bit_Extender bit_extender_2
  assign bit_extender_3_out = {{16{currentInstr_15_0[15]}}, currentInstr_15_0};  // Bit_Extender bit_extender_3
  _32bit_adder u_32bit_adder_1 (.inputA(bit_extender_1_out), .inputB(32'h1), .result(n32bit_adder_1_result));
  not not_1 (not_1_out, IfJ[1]);
  _32bit_adder u_32bit_adder_2 (
    .inputA(bit_extender_3_out), .inputB(bit_extender_1_out), .result(n32bit_adder_2_result));
  and and_1 (and_1_out, IfJ[0], not_1_out);
  and and_2 (and_2_out, IfBeq, Zero);
  Multiplexer #(.select(2), .width(32), .enable("false")) multiplexer_1 (
    .in0(n32bit_adder_1_result), .in1(n32bit_adder_2_result), .in2(bit_extender_2_out),
    .in3({undriven, rs[31:2]}), .out(multiplexer_1_out), .sel(or_2_out));
  or or_1 (or_2_out[1], IfJ[1], and_1_out);
  or or_2 (or_2_out[0], and_1_out, and_2_out);
  SpecialPC specialpc_1 (
    .Input30(multiplexer_1_out[29:0]), .en(not_2_out), .clk(clk), .reset(reset), .Low8(currentPC[9:2]),
    .High22(currentPC[31:10]));
  not not_2 (not_2_out, nen);
  Register #(.width(32)) register_1 (
    .D(CurInstr), .en(not_2_out), .Q({LastInstr, currentInstr_15_0}), .clk(clk), .clr(reset));
  ROM #(.dataWidth(32)) rom_1 (.addr(currentPC[9:2]), .data(CurInstr));  // open: sel

  assign currentPC[1:0] = 2'b00;

  // Other names for the same wires on the sheet: LastInstr[15:0] = currentInstr_15_0;
  //   currentPC30[29:0] = currentPC[31:2]

  // Notes on the sheet:
  //   contents of rom_1 (hex, n*v repeats v):
  //   341a0001 341b0004 341d0020 ac1d0000 b021 b821 34040f0f 34850080 34861111 34870040 afa50000 3bbe821
  //   afa60000 37de821 afa70000 1b4821 13de821 8c080020 35094444 afa90000 3bbe821 c000c67 2fab821 afa90000
  //   3bbe821 1284821 1285021 1285821 afaa0000 3bbe821 afab0000 3bbe821 34090004 ad240000 ad250004
  //   340a0008 8d490000 8d4b0000 afa90000 3bbe821 afab0000 3bbe821 8fa8fff4 11090002 2fab821 2dab021
  //   8fa8fffc 11280002 2fab821 2dab021 804021 a04821 11280002 2fab821 2dab021 c04021 c04821 11090002
  //   2fab821 2dab021 8fa8fffc 1084821 afa90000 3bbe821 8c080000 8d090000 afa90000 3bbe821 ac1d0000
  //   3bbe821 8c080000 ad080000 c000c6b 2fab821 1f4821 34080018 1284821 c821 c000c71 2fab821 340800d4
  //   3e84821 c000c78 2fab821 34080050 3e84821 c000c7e 2fab821 c000c83 2fab821 c000c88 2fab821 c000c8b
  //   2fab821 c000c9c 2fab821 afb70000 3bbe821 afb60000 3bbe821 8000c64 c821 c821 37e90056 3e00008 2fab821
  //   c821 8fe9cf00 afa90000 3bbe821 3e00008 2fab821 c821 c821 113f0002 2fab821 2dab021 3e00008 2fab821
  //   c821 113f0002 2fab821 2dab021 3e00008 2fab821 c821 13e90002 2fab821 2dab021 3e00008 2fab821 3ff4021
  //   afa80000 3bbe821 3e00008 2fab821 affdcea0 3e00008 2fab821 afbf0000 3bbe821 3fbf823 c000c93 2fab821
  //   8fbffff8 3e00008 2fab821 afbf0000 3bbe821 34080008 3e8f821 c821 c821 3e8f823 3e00008 2fab821
  //   34083000 3e8f823 afbf0000 3bbe821 37ff3000 3e00008 2fab821
endmodule

module Extender (
  input  [15:0] \input ,
  input  [1:0] ExtOp,
  output [31:0] \output 
);

  wire [31:0] bit_extender_1_out, bit_extender_2_out;

  assign bit_extender_1_out = {{16{1'b0}}, \input };  // Bit_Extender bit_extender_1
  assign bit_extender_2_out = {{16{\input [15]}}, \input };  // Bit_Extender bit_extender_2
  Multiplexer #(.select(2), .width(32), .enable("false")) multiplexer_1 (
    .in0(bit_extender_1_out), .in1(bit_extender_2_out), .in2({\input , {16{1'b0}}}), .out(\output ),
    .sel(ExtOp));  // open: in3
endmodule

module SpecialPC (
  input  [29:0] Input30,
  input  en,
  input  clk,
  input  reset,
  output [7:0] Low8,
  output [21:0] High22
);

  wire [1:0] not_1_out, register_2_q;

  Register #(.width(18)) register_1 (.D(Input30[29:12]), .en(en), .Q(High22[21:4]), .clk(clk), .clr(reset));
  assign not_1_out = ~Input30[11:10];  // NOT_Gate not_1, 2 bits wide
  assign High22[3:2] = ~register_2_q;  // NOT_Gate not_2, 2 bits wide
  Register #(.width(2)) register_2 (.D(not_1_out), .en(en), .Q(register_2_q), .clk(clk), .clr(reset));
  Register #(.width(2)) register_3 (.D(Input30[9:8]), .en(en), .Q(High22[1:0]), .clk(clk), .clr(reset));
  Register register_4 (.D(Input30[7:0]), .en(en), .Q(Low8), .clk(clk), .clr(reset));
endmodule

module ID_EX (
  input  in_1,
  input  in_2,
  input  in_3,
  input  [1:0] in_4,
  input  [1:0] in_5,
  input  [1:0] in_6,
  input  [31:0] in_7,
  input  [31:0] in_8,
  input  [31:0] in_9,
  input  [31:0] in_10,
  input  [4:0] in_11,
  input  [4:0] in_12,
  input  [4:0] in_13,
  input  nen,
  input  clk,
  input  reset,
  output out_17,
  output out_18,
  output out_19,
  output [1:0] out_20,
  output [1:0] out_21,
  output [1:0] out_22,
  output [31:0] out_23,
  output [31:0] out_24,
  output [31:0] out_25,
  output [31:0] out_26,
  output [4:0] out_27,
  output [4:0] out_28,
  output [4:0] out_29
);

  Register #(.width(1)) ALUSrc (.D(in_1), .en(nen), .Q(out_17), .clk(clk), .clr(reset));
  Register #(.width(1)) RegWrite (.D(in_2), .en(nen), .Q(out_18), .clk(clk), .clr(reset));
  Register #(.width(1)) MemWrite (.D(in_3), .en(nen), .Q(out_19), .clk(clk), .clr(reset));
  Register #(.width(2)) Mem2Reg_1_0 (.D(in_4), .en(nen), .Q(out_20), .clk(clk), .clr(reset));
  Register #(.width(2)) RegDst_1_0 (.D(in_5), .en(nen), .Q(out_21), .clk(clk), .clr(reset));
  Register #(.width(2)) ALUOP_1_0 (.D(in_6), .en(nen), .Q(out_22), .clk(clk), .clr(reset));
  Register #(.width(32)) PC_4 (.D(in_7), .en(nen), .Q(out_23), .clk(clk), .clr(reset));
  Register #(.width(32)) IDRD1 (.D(in_8), .en(nen), .Q(out_24), .clk(clk), .clr(reset));
  Register #(.width(32)) IDRD2 (.D(in_9), .en(nen), .Q(out_25), .clk(clk), .clr(reset));
  Register #(.width(32)) Imm (.D(in_10), .en(nen), .Q(out_26), .clk(clk), .clr(reset));
  Register #(.width(5)) IDRS (.D(in_11), .en(nen), .Q(out_27), .clk(clk), .clr(reset));
  Register #(.width(5)) IDRT (.D(in_12), .en(nen), .Q(out_28), .clk(clk), .clr(reset));
  Register #(.width(5)) IDRD (.D(in_13), .en(nen), .Q(out_29), .clk(clk), .clr(reset));
endmodule

module EX_MEM (
  input  in_1,
  input  in_2,
  input  [1:0] in_3,
  input  [31:0] in_4,
  input  [31:0] in_5,
  input  [31:0] in_6,
  input  [4:0] in_7,
  input  [4:0] in_8,
  input  nen,
  input  clk,
  input  reset,
  output out_12,
  output out_13,
  output [1:0] out_14,
  output [31:0] out_15,
  output [31:0] out_16,
  output [31:0] out_17,
  output [4:0] out_18,
  output [4:0] out_19
);

  Register #(.width(1)) RegWrite (.D(in_1), .en(nen), .Q(out_12), .clk(clk), .clr(reset));
  Register #(.width(1)) MemWrite (.D(in_2), .en(nen), .Q(out_13), .clk(clk), .clr(reset));
  Register #(.width(2)) Mem2Reg_1_0 (.D(in_3), .en(nen), .Q(out_14), .clk(clk), .clr(reset));
  Register #(.width(32)) PC_4 (.D(in_4), .en(nen), .Q(out_15), .clk(clk), .clr(reset));
  Register #(.width(32)) ALUresult (.D(in_5), .en(nen), .Q(out_16), .clk(clk), .clr(reset));
  Register #(.width(32)) WriteData (.D(in_6), .en(nen), .Q(out_17), .clk(clk), .clr(reset));
  Register #(.width(5)) rt (.D(in_7), .en(nen), .Q(out_18), .clk(clk), .clr(reset));
  Register #(.width(5)) WriteReg (.D(in_8), .en(nen), .Q(out_19), .clk(clk), .clr(reset));
endmodule

module MEM_WB (
  input  in_1,
  input  [1:0] in_2,
  input  [31:0] in_3,
  input  [31:0] in_4,
  input  [31:0] in_5,
  input  [4:0] in_6,
  input  nen,
  input  clk,
  input  reset,
  output out_10,
  output [1:0] out_11,
  output [31:0] out_12,
  output [31:0] out_13,
  output [31:0] out_14,
  output [4:0] out_15
);

  Register #(.width(1)) RegWrite (.D(in_1), .en(nen), .Q(out_10), .clk(clk), .clr(reset));
  Register #(.width(2)) Mem2Reg_1_0 (.D(in_2), .en(nen), .Q(out_11), .clk(clk), .clr(reset));
  Register #(.width(32)) PC_4 (.D(in_3), .en(nen), .Q(out_12), .clk(clk), .clr(reset));
  Register #(.width(32)) MemRead (.D(in_4), .en(nen), .Q(out_13), .clk(clk), .clr(reset));
  Register #(.width(32)) ALUresult (.D(in_5), .en(nen), .Q(out_14), .clk(clk), .clr(reset));
  Register #(.width(5)) WriteReg (.D(in_6), .en(nen), .Q(out_15), .clk(clk), .clr(reset));
endmodule

module Stall_Unit (
  input  [4:0] ID_rs,
  input  [4:0] ID_rt,
  input  [1:0] ID_EX_MemReg,
  input  [4:0] ID_EX_rt,
  input  [4:0] ID_EX_rd,
  input  [1:0] ID_EX_RegDst,
  input  [4:0] EX_Mem_WriteReg,
  input  ID_EX_RegWrite,
  input  beq,
  input  [1:0] IfJ,
  input  [1:0] EX_Mem_MemReg,
  output stall
);

  wire and_1_out, and_2_out, and_3_out, and_4_out, and_5_out, beq_or_jr, comparator_1_eq, comparator_2_eq,
       comparator_3_eq, comparator_4_eq, comparator_5_eq, comparator_6_eq, comparator_7_eq, comparator_8_eq,
       comparator_9_eq, comparator_10_eq, comparator_11_eq, equal_rd, equal_rt, equal_WriteReg, or_5_out;

  or or_1 (beq_or_jr, beq, comparator_1_eq);
  Comparator #(.width(2), .mode("unsigned")) comparator_1 (.a(IfJ), .b(2'b10), .eq(comparator_1_eq));  // open: gt, lt
  Comparator #(.width(5), .mode("unsigned")) comparator_2 (
    .a(ID_rs), .b(ID_EX_rt), .eq(comparator_2_eq));  // open: gt, lt
  Comparator #(.width(5), .mode("unsigned")) comparator_3 (
    .a(ID_rs), .b(ID_EX_rd), .eq(comparator_3_eq));  // open: gt, lt
  Comparator #(.width(5), .mode("unsigned")) comparator_4 (
    .a(ID_rs), .b(EX_Mem_WriteReg), .eq(comparator_4_eq));  // open: gt, lt
  Comparator #(.width(5), .mode("unsigned")) comparator_5 (
    .a(ID_rt), .b(ID_EX_rt), .eq(comparator_5_eq));  // open: gt, lt
  Comparator #(.width(5), .mode("unsigned")) comparator_6 (
    .a(ID_rt), .b(ID_EX_rd), .eq(comparator_6_eq));  // open: gt, lt
  Comparator #(.width(5), .mode("unsigned")) comparator_7 (
    .a(ID_rt), .b(EX_Mem_WriteReg), .eq(comparator_7_eq));  // open: gt, lt
  or or_2 (equal_rt, comparator_2_eq, comparator_5_eq);
  or or_3 (equal_rd, comparator_3_eq, comparator_6_eq);
  or or_4 (equal_WriteReg, comparator_4_eq, comparator_7_eq);
  Comparator #(.width(2), .mode("unsigned")) comparator_8 (
    .a(ID_EX_RegDst), .b(2'b00), .eq(comparator_8_eq));  // open: gt, lt
  Comparator #(.width(2), .mode("unsigned")) comparator_9 (
    .a(ID_EX_RegDst), .b(2'b01), .eq(comparator_9_eq));  // open: gt, lt
  and and_1 (and_1_out, equal_rt, comparator_8_eq);
  and and_2 (and_2_out, comparator_9_eq, equal_rd);
  Comparator #(.width(2), .mode("unsigned")) comparator_10 (
    .a(EX_Mem_MemReg), .b(2'b01), .eq(comparator_10_eq));  // open: gt, lt
  Comparator #(.width(2), .mode("unsigned")) comparator_11 (
    .a(ID_EX_MemReg), .b(2'b01), .eq(comparator_11_eq));  // open: gt, lt
  or or_5 (or_5_out, and_1_out, and_2_out);
  and and_3 (and_3_out, comparator_10_eq, equal_WriteReg, beq_or_jr);
  and and_4 (and_4_out, equal_rt, comparator_11_eq);
  and and_5 (and_5_out, or_5_out, ID_EX_RegWrite, beq_or_jr);
  or or_6 (stall, and_4_out, and_5_out, and_3_out);
endmodule

module Forward_Unit (
  input  [4:0] ID_EX_rs,
  input  [4:0] ID_EX_rt,
  input  [4:0] Ex_MEM_WriteReg,
  input  RegWriteM,
  input  [1:0] Mem2RegM,
  input  [4:0] MEM_WB_WriteReg,
  input  RegWriteWB,
  input  [4:0] Ex_MEM_rt,
  input  MemWriteM,
  input  beq,
  input  [1:0] IfJ,
  input  [4:0] ID_rs,
  input  [4:0] ID_rt,
  output [1:0] FowardAE,
  output [1:0] FowardBE,
  output FowardWData_M,
  output [1:0] FowardAD,
  output [1:0] FowardBD
);

  wire _10_2_out, _10_3_out, _10_4_out, _10_out, comparator_2_eq, comparator_3_eq, comparator_4_eq,
       comparator_5_eq, comparator_6_eq, comparator_7_eq, comparator_8_eq, comparator_9_eq, comparator_10_eq,
       comparator_11_eq, jr, jr____beq, not_1_out, not_2_out, not_3_out, not_4_out, RW_M____MEMReg;

  or or_1 (jr____beq, beq, jr);
  Comparator #(.width(2), .mode("unsigned")) comparator_1 (.a(IfJ), .b(2'b01), .eq(jr));  // open: gt, lt
  Comparator #(.width(5), .mode("unsigned")) comparator_2 (
    .a(ID_EX_rs), .b(Ex_MEM_WriteReg), .eq(comparator_2_eq));  // open: gt, lt
  Comparator #(.width(5), .mode("unsigned")) comparator_3 (
    .a(ID_EX_rs), .b(MEM_WB_WriteReg), .eq(comparator_3_eq));  // open: gt, lt
  Comparator #(.width(5), .mode("unsigned")) comparator_4 (
    .a(ID_EX_rt), .b(Ex_MEM_WriteReg), .eq(comparator_4_eq));  // open: gt, lt
  Comparator #(.width(5), .mode("unsigned")) comparator_5 (
    .a(ID_EX_rt), .b(MEM_WB_WriteReg), .eq(comparator_5_eq));  // open: gt, lt
  and and_1 (RW_M____MEMReg, RegWriteM, comparator_6_eq);
  Comparator #(.width(2), .mode("unsigned")) comparator_6 (
    .a(Mem2RegM), .b(2'b00), .eq(comparator_6_eq));  // open: gt, lt
  and and_2 (FowardWData_M, RegWriteWB, comparator_7_eq, MemWriteM);
  Comparator #(.width(5), .mode("unsigned")) comparator_7 (
    .a(MEM_WB_WriteReg), .b(Ex_MEM_rt), .eq(comparator_7_eq));  // open: gt, lt
  Comparator #(.width(5), .mode("unsigned")) comparator_8 (
    .a(ID_rs), .b(Ex_MEM_WriteReg), .eq(comparator_8_eq));  // open: gt, lt
  Comparator #(.width(5), .mode("unsigned")) comparator_9 (
    .a(ID_rs), .b(MEM_WB_WriteReg), .eq(comparator_9_eq));  // open: gt, lt
  Comparator #(.width(5), .mode("unsigned")) comparator_10 (
    .a(ID_rt), .b(Ex_MEM_WriteReg), .eq(comparator_10_eq));  // open: gt, lt
  Comparator #(.width(5), .mode("unsigned")) comparator_11 (
    .a(ID_rt), .b(MEM_WB_WriteReg), .eq(comparator_11_eq));  // open: gt, lt
  and _01 (FowardAD[0], RW_M____MEMReg, jr____beq, comparator_8_eq);
  and _10 (_10_out, comparator_9_eq, RegWriteWB);
  and _01_2 (FowardBD[0], RW_M____MEMReg, jr, comparator_10_eq);
  and _10_2 (_10_2_out, comparator_11_eq, RegWriteWB);
  and _01_3 (FowardAE[0], comparator_2_eq, RW_M____MEMReg);
  and _10_3 (_10_3_out, comparator_3_eq, RegWriteWB);
  and _01_4 (FowardBE[0], comparator_4_eq, RW_M____MEMReg);
  and _10_4 (_10_4_out, comparator_5_eq, RegWriteWB);
  not not_1 (not_1_out, FowardAD[0]);
  not not_2 (not_2_out, FowardBD[0]);
  not not_3 (not_3_out, FowardAE[0]);
  not not_4 (not_4_out, FowardBE[0]);
  and and_3 (FowardAD[1], not_1_out, _10_out);
  and and_4 (FowardBD[1], not_2_out, _10_2_out);
  and and_5 (FowardAE[1], not_3_out, _10_3_out);
  and and_6 (FowardBE[1], not_4_out, _10_4_out);

  // Other names for the same wires on the sheet: RegWri_WB = RegWriteWB; WR_M[4:0] = Ex_MEM_WriteReg;
  //   WR_W[4:0] = MEM_WB_WriteReg
endmodule
